# Fritzing sketch wiringFor3ServoMotors (saved by Fritzing 0.9.2b)
breadboards: 1

parts:
  パーツ1 = Arduino Nano (Rev3.0)
  J1 = Basic Servo
  U1 = LIPO-1000mAh [package=lipo-1000]
  J2 = Basic Servo
  J3 = Basic Servo

nets:
  GND: パーツ1.GND, J1.gnd, U1.-, J2.gnd, J3.gnd
  N1: パーツ1.D3, J1.pulse
  N2: パーツ1.D5, J3.pulse
  N3: パーツ1.D11/MOSI, J2.pulse
  VCC: パーツ1.VIN, J1.vcc, U1.+, J2.vcc, J3.vcc
